# Fritzing sketch camping base station (saved by Fritzing 0.9.2b)
breadboards: 1

parts:
  Transceiver1 = nRF24L01 [package=module]
  Part1 = Arduino Nano (Rev3.0)
  LED1 = LED - 5mm [color="Red (633nm)" package="5 mm [THT]"]  # not connected
  S1 = Pushbutton [package="[THT]"]
  R1 = Resistor [tolerance=±5% resistance=220 package=THT]  # not connected
  R2 = Resistor [tolerance=±5% resistance=10k package=THT]

nets:
  GND: Transceiver1.GND, Part1.GND, R2.Pin_0
  VCC: Transceiver1.VCC, Part1.3V3
  N1: Transceiver1.CE, Part1.D7
  N2: Transceiver1.CSN, Part1.D8
  N3: Transceiver1.SCK, Part1.D13/SCK
  N4: Transceiver1.MOSI, Part1.D11/MOSI
  N5: Transceiver1.MISO, Part1.D12/MISO
  N6: Part1.D2, R2.Pin_1
  N7: Part1.5V, S1.Pin_1, S1.Pin_2

custom parts:
  nRF24L01: nRF24L01 module
