# Fritzing sketch camping lights satellite (saved by Fritzing 0.9.2b)
breadboards: 1

parts:
  U1 = NodeMCU V1.0
  Transceiver1 = nRF24L01 [package=module]
  LED1 = LED - 5mm [color="Red (633nm)" package="5 mm [THT]"]
  R1 = Resistor [tolerance=±5% resistance=220 package=THT]

nets:
  N1: U1.D1, R1.Pin_1
  N2: U1.D2, Transceiver1.CSN
  N3: U1.D4, Transceiver1.CE
  3V3: U1.3V3, Transceiver1.VCC
  GND: U1.GND, Transceiver1.GND, LED1.cathode
  N4: U1.D5, Transceiver1.SCK
  N5: U1.D6, Transceiver1.MISO
  N6: U1.D7, Transceiver1.MOSI
  N7: LED1.anode, R1.Pin_0

custom parts:
  NodeMCU V1.0: ESP8266 based NodeMCU
  nRF24L01: nRF24L01 module
